# Fritzing sketch Cycle 1 (saved by Fritzing 0.9.3b)
breadboards: 1

parts:
  Microprocessor = Photon [part_number="Particle Photon"]
  Passive_Infrared_Sensor = PIR sensor

nets:
  GND: Microprocessor.GND, Passive_Infrared_Sensor.GND
  VIN: Microprocessor.VIN, Passive_Infrared_Sensor.VDD
  N1: Microprocessor.D2, Passive_Infrared_Sensor.SIG
