# Fritzing sketch PCB Rev 1.0c (saved by Fritzing 0.9.3b)
circuit board: 13.2cm x 11cm

parts:
  Photon = Photon [part_number="Base | Module 1"]
  Left_Switch = SWITCH-MOMENTARY-2 [package=tactile-pth-12mm]
  Centre_Switch = SWITCH-MOMENTARY-2 [package=tactile-pth-12mm]
  Right_Switch = SWITCH-MOMENTARY-2 [package=tactile-pth-12mm]
  Neopixel_RGB = Adafruit Breadboard-Friendly NeoPixel [part_number="Adafruit #1312"]
  Piezo_Buzzer = Piezo Speaker
  OLED_Display = OLED Monochrome 128x64 0.96 inch [part_number=326]
  FRAM = I2C Non-Volatile FRAM 32KB
  Logic_Level = Adafruit 4-channel I2C-safe Bi-directional Logic Level Converter [part_number="Adafruit #757"]
  SMP_Header = Header 5x2 [package=avr_icsp]
  Door_Switch = Screw terminal - 2 pins [package=THT]
  3_3v_Buck = Adafruit LM3671 Buck Converter [part_number="Adafruit #2745"]
  GND = Header 1 [package=1x01_offset]
  GND_2 = Header 1 [package=1x01_offset]  # not connected
  On = Header 1 [package=1x01_offset]  # not connected
  SW = Header 1 [package=1x01_offset]

nets:
  N1: Photon.A0, SMP_Header.8
  N2: Photon.A1, FRAM.WP
  N3: Photon.A2, Right_Switch.1
  N4: Photon.A3, SMP_Header.7
  N5: Photon.A4, Door_Switch.pin1
  N6: Photon.A5, OLED_Display.RESET
  N7: Photon.DAC, SMP_Header.10
  N8: Photon.WKP, Piezo_Buzzer.pin2
  GND: Photon.GND, Left_Switch.2, Centre_Switch.2, Right_Switch.2, Neopixel_RGB.GND, Piezo_Buzzer.pin1, OLED_Display.GND, FRAM.GND, Logic_Level.GND, SMP_Header.2, Door_Switch.pin2, 3_3v_Buck.GND, GND.1
  VIN: Photon.VIN, Neopixel_RGB.VDD, Logic_Level.HV, SMP_Header.1
  N9: Photon.D0, OLED_Display.MOSI_SDA, FRAM.SDA, SMP_Header.4
  N10: Photon.D1, OLED_Display.SCLK_SCK, FRAM.SCL, SMP_Header.6
  N11: Photon.D2, Logic_Level.A3
  N12: Photon.D3, Logic_Level.A2
  N13: Photon.D4, Logic_Level.A1
  N14: Photon.D5, Centre_Switch.1
  N15: Photon.D6, Left_Switch.1
  N16: Photon.D7, SMP_Header.9
  N17: Photon.VBAT, 3_3v_Buck.3.3V
  3V3: Photon.3V3, OLED_Display.VIN, FRAM.VCC, Logic_Level.LV
  N18: Neopixel_RGB.IN, Logic_Level.B2
  N19: Logic_Level.B3, SMP_Header.3
  N20: Logic_Level.B1, SMP_Header.5
  N21: 3_3v_Buck.VIN, SW.1

notes:
  IoT Sensor
  Rev. 1.0c
  Samuel Herring
  IoT Room Status, A-Level Project Internet of Things Room Sensor to monitor movement and provide visual feedback., 1.0c

custom parts:
  Adafruit Breadboard-Friendly NeoPixel: This is the easiest way possible to add small, bright RGB pixels to your project. We took the same technology from our Flora NeoPixels and made them breadboard friendly, with two rows of 3 x 0.1" spaced header on each side for easy soldering, chaining and breadboarding. These ultra-bright LEDs have a constant-current driver cooked right into the LED package! The pixels are chainable - so you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
  OLED Monochrome 128x64 0.96 inch: These displays are small, only about 1" diameter, but very readable due to the high contrast of an OLED display. This display is made of 128x64 individual white OLED pixels, each one is turned on or off by the controller chip. Because the display makes its own light, no backlight is required. This reduces the power required to run the OLED and is why the display has such high contrast; we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
  I2C Non-Volatile FRAM 32KB: With our I2C FRAM breakout board you can add some FRAM storage to your next DIY project. FRAM allows for a lower power usage and a faster write performance. It's excellent for low-power or inconsistent-power datalogging or data buffering where you want to stream data fast while also keeping the data when there's no power. Unlike Flash or EEPROM there's no pages to worry about. Each byte can be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
  Adafruit 4-channel I2C-safe Bi-directional Logic Level Converter: Because the Arduino (and Basic Stamp) are 5V devices, and most modern sensors, displays, flash cards and modes are 3.3V-only, many makers find that they need to perform level shifting/conversion to protect the 3.3V device from 5V. We do have some other handy level shifters in the shop, from the DIP 74LVC245 to the fancy bi-directional TXB0108. However, neither of these are happy to work with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
  Adafruit LM3671 Buck Converter: Your power supply problems just got SUPER SOLVED! This 3.3V Buck Converter Breakout board is great for supplying power to low voltage circuits from a single Li-Ion cell battery or USB power. This chip provides up to 600-mA load current across the entire input voltage range of 3.5 to 5.5V. Great for your portable project, we made this "pin compatible" with the LM1117-3.3V TO-220 chip so you can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
